// Logisim project (A+B).(A'+B).circ as structural Verilog: 1 circuit, main circuit main
module main (
  input  in_1,
  input  in_2,
  output out_3
);

  wire not_1_out, or_1_out, or_2_out;

  not not_1 (not_1_out, in_1);
  or or_1 (or_1_out, in_1, in_2);
  or or_2 (or_2_out, not_1_out, in_1);
  and and_1 (out_3, or_1_out, or_2_out);
endmodule
