// Logisim project Full_Adder_SUM.circ as structural Verilog: 1 circuit, main circuit main
module main (
  input  in_1,
  input  in_2,
  output out_3
);

  wire and_1_out, and_2_out, and_3_out, and_4_out;

  and and_1 (and_1_out, in_1, in_2);
  and and_2 (and_2_out, in_1, in_2);
  and and_3 (and_3_out, in_1, in_2);
  and and_4 (and_4_out, in_1, in_2);
  or or_1 (out_3, and_1_out, and_2_out, and_3_out, and_4_out);
endmodule
